// Logisim project main.circ as structural Verilog: 3 circuits, main circuit main
module main (
  input  [3:0] in_1,
  input  [3:0] in_2
);

  _4_Bit_Ripple_Carry_Adder u_4_bit_ripple_carry_adder_1 (.A(in_1), .B(in_2));  // open: CO, O, CI
endmodule

module Full_Adder (
  input  A,
  input  B,
  input  CI,
  output S,
  output CO
);

  wire and_1_out, and_2_out, or_1_out, xor_1_out;

  xor xor_1 (xor_1_out, A, B);
  and and_1 (and_1_out, CI, or_1_out);
  or or_1 (or_1_out, A, B);
  and and_2 (and_2_out, A, B);
  xor xor_2 (S, xor_1_out, CI);
  or or_2 (CO, and_1_out, and_2_out);
endmodule

module _4_Bit_Ripple_Carry_Adder (
  input  [3:0] A,
  input  CI,
  input  [3:0] B,
  output CO,
  output [3:0] O
);

  wire full_adder_2_co, full_adder_3_co, full_adder_4_co;

  Full_Adder full_adder_1 (.S(O[3]), .CO(CO), .B(B[3]), .CI(full_adder_2_co), .A(A[3]));
  Full_Adder full_adder_2 (.S(O[2]), .CO(full_adder_2_co), .B(B[2]), .CI(full_adder_3_co), .A(A[2]));
  Full_Adder full_adder_3 (.S(O[1]), .CO(full_adder_3_co), .B(B[1]), .CI(full_adder_4_co), .A(A[1]));
  Full_Adder full_adder_4 (.S(O[0]), .CO(full_adder_4_co), .B(B[0]), .CI(CI), .A(A[0]));
endmodule
